// Logisim project TermProject_Circuit_Design.circ as structural Verilog: 11 circuits, main circuit Register File
module Register_File (
  input  [15:0] INPUT,
  input  [2:0] SR1,
  input  [2:0] DR,
  input  [2:0] SR2,
  input  WI,
  input  Clock,
  input  Reset,
  output [15:0] out_8,
  output [15:0] OUTPUT1,
  output [15:0] out_10,
  output [15:0] out_11,
  output [15:0] out_12,
  output [15:0] out_13,
  output [15:0] OUTPUT2,
  output [15:0] out_15,
  output [15:0] out_16,
  output [15:0] out_17
);

  wire and_1_out, and_2_out, and_3_out, and_4_out, and_5_out, and_6_out, and_7_out, and_8_out,
       decoder_1_out0, decoder_1_out1, decoder_1_out2, decoder_1_out3, decoder_1_out4, decoder_1_out5,
       decoder_1_out6, decoder_1_out7;

  Decoder #(.select(3), .enable("false")) decoder_1 (
    .out0(decoder_1_out0), .out1(decoder_1_out1), .out2(decoder_1_out2), .out3(decoder_1_out3),
    .out4(decoder_1_out4), .out5(decoder_1_out5), .out6(decoder_1_out6), .out7(decoder_1_out7), .sel(DR));
  and and_1 (and_1_out, decoder_1_out0, WI);
  and and_2 (and_2_out, decoder_1_out1, WI);
  and and_3 (and_3_out, decoder_1_out2, WI);
  and and_4 (and_4_out, decoder_1_out3, WI);
  and and_5 (and_5_out, decoder_1_out4, WI);
  and and_6 (and_6_out, decoder_1_out5, WI);
  and and_7 (and_7_out, decoder_1_out6, WI);
  and and_8 (and_8_out, decoder_1_out7, WI);
  _16_Bit_Register u_16_bit_register_1 (.D(INPUT), .Enable(and_1_out), .Q(out_8), .clk(Clock), .Clear(Reset));
  _16_Bit_Register u_16_bit_register_2 (.D(INPUT), .Enable(and_2_out), .Q(out_10), .clk(Clock), .Clear(Reset));
  _16_Bit_Register u_16_bit_register_3 (.D(INPUT), .Enable(and_3_out), .Q(out_11), .clk(Clock), .Clear(Reset));
  _16_Bit_Register u_16_bit_register_4 (.D(INPUT), .Enable(and_4_out), .Q(out_12), .clk(Clock), .Clear(Reset));
  _16_Bit_Register u_16_bit_register_5 (.D(INPUT), .Enable(and_5_out), .Q(out_13), .clk(Clock), .Clear(Reset));
  _16_Bit_Register u_16_bit_register_6 (.D(INPUT), .Enable(and_6_out), .Q(out_15), .clk(Clock), .Clear(Reset));
  _16_Bit_Register u_16_bit_register_7 (.D(INPUT), .Enable(and_7_out), .Q(out_16), .clk(Clock), .Clear(Reset));
  _16_Bit_Register u_16_bit_register_8 (.D(INPUT), .Enable(and_8_out), .Q(out_17), .clk(Clock), .Clear(Reset));
  Multiplexer #(.select(3), .width(16), .enable("false")) multiplexer_1 (
    .in0(out_8), .in1(out_10), .in2(out_11), .in3(out_12), .in4(out_13), .in5(out_15), .in6(out_16),
    .in7(out_17), .out(OUTPUT2), .sel(SR2));
  Multiplexer #(.select(3), .width(16), .enable("false")) multiplexer_2 (
    .in0(out_8), .in1(out_10), .in2(out_11), .in3(out_12), .in4(out_13), .in5(out_15), .in6(out_16),
    .in7(out_17), .out(OUTPUT1), .sel(SR1));
endmodule

module Full_Adder (
  input  A,
  input  B,
  input  Carry_in,
  output Result,
  output Carry_out
);

  wire and_1_out, and_2_out, or_1_out;

  and and_1 (and_1_out, A, or_1_out);
  or or_1 (or_1_out, B, Carry_in);
  xor xor_1 (Result, A, B, Carry_in);
  and and_2 (and_2_out, ~A, B, Carry_in);  // AND_Gate
  or or_2 (Carry_out, and_2_out, and_1_out);
endmodule

module Adder (
  input  [15:0] Number1,
  input  [15:0] Number2,
  output Overflow_Flag,
  output [15:0] Result
);

  wire full_adder_2_carry_out, full_adder_3_carry_out, full_adder_4_carry_out, full_adder_5_carry_out,
       full_adder_6_carry_out, full_adder_7_carry_out, full_adder_8_carry_out, full_adder_9_carry_out,
       full_adder_10_carry_out, full_adder_11_carry_out, full_adder_12_carry_out, full_adder_13_carry_out,
       full_adder_14_carry_out, full_adder_15_carry_out, full_adder_16_carry_out;

  Full_Adder full_adder_1 (
    .A(full_adder_2_carry_out), .B(Number2[15]), .Carry_in(Number1[15]), .Result(Result[15]),
    .Carry_out(Overflow_Flag));
  Full_Adder full_adder_2 (
    .A(full_adder_3_carry_out), .B(Number2[14]), .Carry_in(Number1[14]), .Result(Result[14]),
    .Carry_out(full_adder_2_carry_out));
  Full_Adder full_adder_3 (
    .A(full_adder_4_carry_out), .B(Number2[13]), .Carry_in(Number1[13]), .Result(Result[13]),
    .Carry_out(full_adder_3_carry_out));
  Full_Adder full_adder_4 (
    .A(full_adder_5_carry_out), .B(Number2[12]), .Carry_in(Number1[12]), .Result(Result[12]),
    .Carry_out(full_adder_4_carry_out));
  Full_Adder full_adder_5 (
    .A(full_adder_6_carry_out), .B(Number2[11]), .Carry_in(Number1[11]), .Result(Result[11]),
    .Carry_out(full_adder_5_carry_out));
  Full_Adder full_adder_6 (
    .A(full_adder_7_carry_out), .B(Number2[10]), .Carry_in(Number1[10]), .Result(Result[10]),
    .Carry_out(full_adder_6_carry_out));
  Full_Adder full_adder_7 (
    .A(full_adder_8_carry_out), .B(Number2[9]), .Carry_in(Number1[9]), .Result(Result[9]),
    .Carry_out(full_adder_7_carry_out));
  Full_Adder full_adder_8 (
    .A(full_adder_9_carry_out), .B(Number2[8]), .Carry_in(Number1[8]), .Result(Result[8]),
    .Carry_out(full_adder_8_carry_out));
  Full_Adder full_adder_9 (
    .A(full_adder_10_carry_out), .B(Number2[7]), .Carry_in(Number1[7]), .Result(Result[7]),
    .Carry_out(full_adder_9_carry_out));
  Full_Adder full_adder_10 (
    .A(full_adder_11_carry_out), .B(Number2[6]), .Carry_in(Number1[6]), .Result(Result[6]),
    .Carry_out(full_adder_10_carry_out));
  Full_Adder full_adder_11 (
    .A(full_adder_12_carry_out), .B(Number2[5]), .Carry_in(Number1[5]), .Result(Result[5]),
    .Carry_out(full_adder_11_carry_out));
  Full_Adder full_adder_12 (
    .A(full_adder_13_carry_out), .B(Number2[4]), .Carry_in(Number1[4]), .Result(Result[4]),
    .Carry_out(full_adder_12_carry_out));
  Full_Adder full_adder_13 (
    .A(full_adder_14_carry_out), .B(Number2[3]), .Carry_in(Number1[3]), .Result(Result[3]),
    .Carry_out(full_adder_13_carry_out));
  Full_Adder full_adder_14 (
    .A(full_adder_15_carry_out), .B(Number2[2]), .Carry_in(Number1[2]), .Result(Result[2]),
    .Carry_out(full_adder_14_carry_out));
  Full_Adder full_adder_15 (
    .A(full_adder_16_carry_out), .B(Number2[1]), .Carry_in(Number1[1]), .Result(Result[1]),
    .Carry_out(full_adder_15_carry_out));
  Full_Adder full_adder_16 (
    .A(1'b0), .B(Number2[0]), .Carry_in(Number1[0]), .Result(Result[0]), .Carry_out(full_adder_16_carry_out));
endmodule

module ALU (
  input  [15:0] SR1,
  input  [15:0] SR2,
  input  [6:0] IMM,
  input  [1:0] Alu_Control,
  input  in_5,
  output [15:0] Result
);

  wire adder_1_out, multiplexer_2_out;
  wire [15:0] adder_2_result, and_1_out, multiplexer_1_out;

  Multiplexer #(.width(16), .enable("false")) multiplexer_1 (
    .in0(SR2), .in1({{10{IMM[6]}}, IMM[5:0]}), .out(multiplexer_1_out), .sel(adder_1_out));
  Adder_part #(.width(1)) adder_1 (.a(Alu_Control[1]), .b(Alu_Control[0]), .out(adder_1_out));  // open: cin, cout
  assign and_1_out = SR1 & multiplexer_1_out;  // AND_Gate and_1, 16 bits wide
  Adder adder_2 (.Number1(SR1), .Number2(multiplexer_1_out), .Result(adder_2_result));  // open: Overflow_Flag
  Multiplexer #(.enable("false")) multiplexer_2 (
    .in0(in_5), .in1(Alu_Control[1]), .out(multiplexer_2_out), .sel(adder_1_out));
  Multiplexer #(.width(16), .enable("false")) multiplexer_3 (
    .in0(and_1_out), .in1(adder_2_result), .out(Result), .sel(multiplexer_2_out));
endmodule

module Jump_Condition_Checker (
  input  [2:0] Op_Code,
  input  in_2,
  input  [2:0] CondCheck,
  input  ZF,
  input  CF,
  output JumpConditionResult
);

  wire and_1_out, and_2_out, and_3_out, and_4_out, and_5_out, and_6_out, and_7_out, and_8_out, and_9_out,
       and_10_out, and_11_out, and_12_out, and_13_out, JA, JAE, JB, JBE, JE, or_1_out, or_2_out, or_3_out;

  Decoder #(.select(3), .enable("false")) decoder_1 (
    .out0(JAE), .out4(JA), .out5(JB), .out6(JE), .out7(JBE), .sel(CondCheck));  // open: out1, out2, out3
  and and_1 (and_1_out, ~ZF, CF);  // AND_Gate
  and and_2 (and_2_out, ZF, ~CF);  // AND_Gate
  and and_3 (and_3_out, ~ZF, ~CF);  // AND_Gate
  and and_4 (and_4_out, ZF, ~CF);  // AND_Gate
  and and_5 (and_5_out, ZF, ~CF);  // AND_Gate
  and and_6 (and_6_out, ~ZF, ~CF);  // AND_Gate
  and and_7 (and_7_out, ~ZF, CF);  // AND_Gate
  or or_1 (or_1_out, and_1_out, and_2_out);
  or or_2 (or_2_out, and_3_out, and_4_out);
  and and_8 (and_8_out, and_5_out, JE, in_2);
  and and_9 (and_9_out, and_6_out, JA, in_2);
  and and_10 (and_10_out, and_7_out, JB, in_2);
  and and_11 (and_11_out, or_1_out, JBE, in_2);
  and and_12 (and_12_out, or_2_out, JAE, in_2);
  or or_3 (or_3_out, and_8_out, and_9_out, and_10_out, and_11_out, and_12_out);
  and and_13 (and_13_out, ~Op_Code[0], Op_Code[1], Op_Code[2]);  // AND_Gate
  or or_4 (JumpConditionResult, or_3_out, and_13_out);

  // Other names for the same wires on the sheet: JCC = in_2; i0 = Op_Code[0]; i1 = Op_Code[1]; i2 = Op_Code[2]
endmodule

module Comparator (
  input  isCompare,
  input  [15:0] Number1,
  input  [15:0] Number2,
  input  Clock,
  input  Reset,
  output ZF,
  output CF
);

  wire and_1_out, and_2_out, comparator_1_eq, comparator_1_gt, comparator_1_lt;

  Comparator_part #(.width(16)) comparator_1 (
    .a(Number1), .b(Number2), .gt(comparator_1_gt), .eq(comparator_1_eq), .lt(comparator_1_lt));
  and and_1 (and_1_out, ~comparator_1_gt, comparator_1_eq, ~comparator_1_lt);  // AND_Gate
  and and_2 (and_2_out, ~comparator_1_gt, ~comparator_1_eq, comparator_1_lt);  // AND_Gate
  _1_Bit_Register ZFRegister (.clk(Clock), .D(and_1_out), .Q(ZF), .Enable(isCompare), .Clear(Reset));
  _1_Bit_Register CFRegister (.clk(Clock), .D(and_2_out), .Q(CF), .Enable(isCompare), .Clear(Reset));
endmodule

module CPU (
  input  in_1
);

  wire and_1_out, CF, Clock, control_unit_1_isalu, control_unit_1_jcc, control_unit_1_memoryread,
       control_unit_1_memorywrite, isCompare, JumpConditionResult, nor_1_out, PCSelect, PCWrite,
       WriteRegister, ZF;
  wire [2:0] Destination, multiplexer_2_out, multiplexer_3_out, OpCode;
  wire [9:0] _10BitAddress;
  wire [15:0] adder_1_out, alu_1_result, bit_extender_1_out, multiplexer_1_out, multiplexer_4_out, PC,
       ram_1_data, Reg1, Reg2, register_file_1_out_8;

  assign bit_extender_1_out = {{6{1'b0}}, _10BitAddress};  // Bit_Extender bit_extender_1
  Multiplexer #(.width(16), .enable("false")) multiplexer_1 (
    .in0(16'h1), .in1(bit_extender_1_out), .out(multiplexer_1_out), .sel(and_1_out));
  and and_1 (and_1_out, JumpConditionResult, PCSelect);
  Clock u_Clock (.out(Clock));
  _16_Bit_Register u_16_bit_register_1 (.D(adder_1_out), .Enable(PCWrite), .Q(PC), .clk(nor_1_out), .Clear(in_1));
  Adder_part #(.width(16)) adder_1 (.a(PC), .b(multiplexer_1_out), .out(adder_1_out));  // open: cin, cout
  nor nor_1 (nor_1_out, Clock, in_1);
  ROM #(.addrWidth(16), .dataWidth(16)) rom_1 (.addr(PC), .data({_10BitAddress, Destination, OpCode}), .sel(1'b1));
  Multiplexer #(.width(3), .enable("false")) multiplexer_2 (
    .in0(_10BitAddress[5:3]), .in1(Destination), .out(multiplexer_2_out), .sel(isCompare));
  Multiplexer #(.width(3), .enable("false")) multiplexer_3 (
    .in0(_10BitAddress[2:0]), .in1(Destination), .out(multiplexer_3_out), .sel(control_unit_1_memorywrite));
  Control_Unit control_unit_1 (
    .in_1(OpCode), .WriteRegister(WriteRegister), .MemoryWrite(control_unit_1_memorywrite),
    .MemoryRead(control_unit_1_memoryread), .isALU(control_unit_1_isalu), .isCompare(isCompare),
    .PCSelect(PCSelect), .PCWrite(PCWrite), .Clock(Clock), .JCC(control_unit_1_jcc));  // open: PCRead, InstructionRead
  Multiplexer #(.width(16), .enable("false")) multiplexer_4 (
    .in0(ram_1_data), .in1(alu_1_result), .out(multiplexer_4_out), .sel(control_unit_1_isalu));
  Register_File register_file_1 (
    .SR1(multiplexer_3_out), .SR2(multiplexer_2_out), .INPUT(multiplexer_4_out), .WI(WriteRegister),
    .Clock(Clock), .OUTPUT1(Reg1), .OUTPUT2(Reg2), .DR(Destination), .Reset(in_1),
    .out_8(register_file_1_out_8), .out_10(register_file_1_out_8), .out_11(register_file_1_out_8),
    .out_12(register_file_1_out_8), .out_13(register_file_1_out_8), .out_15(register_file_1_out_8),
    .out_16(register_file_1_out_8), .out_17(register_file_1_out_8));
  ALU alu_1 (
    .SR1(Reg1), .SR2(Reg2), .IMM(_10BitAddress[9:3]), .Alu_Control(OpCode[1:0]), .in_5(_10BitAddress[9]),
    .Result(alu_1_result));
  RAM #(.addrWidth(10), .dataWidth(16), .bus("separate")) ram_1 (
    .addr(_10BitAddress), .din(Reg1), .data(ram_1_data), .str(control_unit_1_memorywrite), .sel(1'b1),
    .clk(Clock), .ld(control_unit_1_memoryread));  // open: clr
  Comparator comparator_1 (
    .Number1(Reg1), .Number2(Reg2), .Clock(Clock), .ZF(ZF), .CF(CF), .isCompare(isCompare), .Reset(in_1));
  Jump_Condition_Checker jump_condition_checker_1 (
    .Op_Code(OpCode), .CondCheck(Destination), .ZF(ZF), .CF(CF), .JumpConditionResult(JumpConditionResult),
    .in_2(control_unit_1_jcc));

  // Other names for the same wires on the sheet: Source1[2:0] = _10BitAddress[2:0]; Source2[2:0] = _10BitAddress[5:3];
  //   Reset = in_1

  // Notes on the sheet:
  //   Instruction Memory
  //   contents of rom_1 (hex, n*v repeats v):
  //   a02 e4a 8210 218 261 95 ac 86 202 43 a7 292 b af 202 ab b7 292 b bf 202 ab 87
  //   Data Memory
endmodule

module Control_Unit (
  input  [2:0] in_1,
  input  Clock,
  output isCompare,
  output WriteRegister,
  output PCSelect,
  output MemoryWrite,
  output MemoryRead,
  output PCRead,
  output InstructionRead,
  output PCWrite,
  output JCC,
  output isALU
);

  wire and_1_out, and_2_out, and_4_out, and_5_out, and_6_out, and_7_out, and_8_out, and_9_out, and_10_out,
       and_11_out, and_12_out, and_13_out, and_14_out, and_16_out, and_17_out, and_19_out, and_22_out,
       and_23_out, and_24_out, and_25_out, or_1_out, or_2_out, or_3_out, or_4_out, State0, State1, State2;
  wire [2:0] adder_1_out;

  and and_1 (and_1_out, in_1[0], ~in_1[1], in_1[2]);  // AND_Gate
  and and_2 (and_2_out, ~State0, State1, ~State2);  // AND_Gate
  and and_3 (MemoryWrite, and_1_out, and_2_out);
  and and_4 (and_4_out, ~in_1[0], ~in_1[1], ~in_1[2]);  // AND_Gate
  and and_5 (and_5_out, ~in_1[0], ~in_1[1], in_1[2]);  // AND_Gate
  and and_6 (and_6_out, in_1[0], ~in_1[1], ~in_1[2]);  // AND_Gate
  and and_7 (and_7_out, ~in_1[0], in_1[1], ~in_1[2]);  // AND_Gate
  and and_8 (and_8_out, ~in_1[0], ~in_1[1], ~in_1[2]);  // AND_Gate
  and and_9 (and_9_out, in_1[0], ~in_1[1], ~in_1[2]);  // AND_Gate
  and and_10 (and_10_out, ~in_1[0], in_1[1], ~in_1[2]);  // AND_Gate
  and and_11 (and_11_out, ~State0, State1, ~State2);  // AND_Gate
  and and_12 (and_12_out, State0, State1, ~State2);  // AND_Gate
  and and_13 (and_13_out, State0, State1, ~State2);  // AND_Gate
  or or_1 (or_1_out, and_11_out, and_12_out);
  or or_2 (or_2_out, and_4_out, and_5_out, and_6_out, and_7_out);
  and and_14 (and_14_out, State0, State1, ~State2);  // AND_Gate
  or or_3 (or_3_out, and_8_out, and_9_out, and_10_out);
  and and_15 (WriteRegister, or_2_out, and_13_out);
  and and_16 (and_16_out, ~in_1[0], ~in_1[1], in_1[2]);  // AND_Gate
  and and_17 (and_17_out, ~State0, State1, ~State2);  // AND_Gate
  and and_18 (isALU, or_3_out, or_1_out);
  or or_4 (or_4_out, and_17_out, and_14_out);
  and and_19 (and_19_out, State0, ~State1, State2);  // AND_Gate
  Register #(.width(3)) register_1 (
    .D(adder_1_out), .Q({State2, State1, State0}), .clk(Clock), .clr(and_19_out));  // open: en
  and and_20 (MemoryRead, and_16_out, or_4_out);
  Adder_part #(.width(3)) adder_1 (.a({State2, State1, State0}), .b(3'b001), .out(adder_1_out));  // open: cin, cout
  and and_21 (JCC, in_1[0], in_1[1], in_1[2]);
  and and_22 (and_22_out, in_1[0], in_1[1], ~in_1[2]);  // AND_Gate
  and and_23 (and_23_out, ~State0, State1, ~State2);  // AND_Gate
  and and_24 (and_24_out, ~in_1[0], in_1[1], in_1[2]);  // AND_Gate
  and and_25 (and_25_out, in_1[0], in_1[1], in_1[2]);
  and and_26 (PCRead, ~State0, ~State1, ~State2);  // AND_Gate
  and and_27 (InstructionRead, State0, ~State1, ~State2);  // AND_Gate
  and and_28 (PCWrite, ~State0, ~State1, State2);  // AND_Gate
  and and_29 (isCompare, and_22_out, and_23_out);
  or or_5 (PCSelect, and_24_out, and_25_out);

  // Other names for the same wires on the sheet: OpCode[2:0] = in_1
endmodule

module D_Flip_Flop (
  input  D,
  input  clk,
  input  Preset,
  input  Enable,
  input  Clear,
  output Q,
  output Q_prime
);

  wire multiplexer_1_out, nand_1_out, nand_2_out, not_1_out, not_2_out, not_3_out;

  Multiplexer #(.enable("false")) multiplexer_1 (.in0(Q), .in1(D), .out(multiplexer_1_out), .sel(Enable));
  not not_1 (not_1_out, Preset);
  not not_2 (not_2_out, multiplexer_1_out);
  not not_3 (not_3_out, Clear);
  nand nand_1 (nand_1_out, multiplexer_1_out, clk);
  nand nand_2 (nand_2_out, clk, not_2_out);
  nand nand_3 (Q, not_1_out, nand_1_out, Q_prime);
  nand nand_4 (Q_prime, Q, nand_2_out, not_3_out);
endmodule

module _16_Bit_Register (
  input  [15:0] D,
  input  Enable,
  input  clk,
  input  Clear,
  output [15:0] Q
);

  D_Flip_Flop_part d_ff_1 (.clk(clk), .D(D[0]), .Q(Q[0]), .preset(1'b0), .en(Enable), .reset(Clear));  // open: Qn
  D_Flip_Flop_part d_ff_2 (.clk(clk), .D(D[1]), .Q(Q[1]), .preset(1'b0), .en(Enable), .reset(Clear));  // open: Qn
  D_Flip_Flop_part d_ff_3 (.clk(clk), .D(D[2]), .Q(Q[2]), .preset(1'b0), .en(Enable), .reset(Clear));  // open: Qn
  D_Flip_Flop_part d_ff_4 (.clk(clk), .D(D[3]), .Q(Q[3]), .preset(1'b0), .en(Enable), .reset(Clear));  // open: Qn
  D_Flip_Flop_part d_ff_5 (.clk(clk), .D(D[4]), .Q(Q[4]), .preset(1'b0), .en(Enable), .reset(Clear));  // open: Qn
  D_Flip_Flop_part d_ff_6 (.clk(clk), .D(D[5]), .Q(Q[5]), .preset(1'b0), .en(Enable), .reset(Clear));  // open: Qn
  D_Flip_Flop_part d_ff_7 (.clk(clk), .D(D[6]), .Q(Q[6]), .preset(1'b0), .en(Enable), .reset(Clear));  // open: Qn
  D_Flip_Flop_part d_ff_8 (.clk(clk), .D(D[7]), .Q(Q[7]), .preset(1'b0), .en(Enable), .reset(Clear));  // open: Qn
  D_Flip_Flop_part d_ff_9 (.clk(clk), .D(D[8]), .Q(Q[8]), .preset(1'b0), .en(Enable), .reset(Clear));  // open: Qn
  D_Flip_Flop_part d_ff_10 (.clk(clk), .D(D[9]), .Q(Q[9]), .preset(1'b0), .en(Enable), .reset(Clear));  // open: Qn
  D_Flip_Flop_part d_ff_11 (.clk(clk), .D(D[10]), .Q(Q[10]), .preset(1'b0), .en(Enable), .reset(Clear));  // open: Qn
  D_Flip_Flop_part d_ff_12 (.clk(clk), .D(D[11]), .Q(Q[11]), .preset(1'b0), .en(Enable), .reset(Clear));  // open: Qn
  D_Flip_Flop_part d_ff_13 (.clk(clk), .D(D[12]), .Q(Q[12]), .preset(1'b0), .en(Enable), .reset(Clear));  // open: Qn
  D_Flip_Flop_part d_ff_14 (.clk(clk), .D(D[13]), .Q(Q[13]), .preset(1'b0), .en(Enable), .reset(Clear));  // open: Qn
  D_Flip_Flop_part d_ff_15 (.clk(clk), .D(D[14]), .Q(Q[14]), .preset(1'b0), .en(Enable), .reset(Clear));  // open: Qn
  D_Flip_Flop_part d_ff_16 (.clk(clk), .D(D[15]), .Q(Q[15]), .preset(1'b0), .en(Enable), .reset(Clear));  // open: Qn
endmodule

module _1_Bit_Register (
  input  D,
  input  Enable,
  input  clk,
  input  Clear,
  output Q
);

  D_Flip_Flop_part d_ff_1 (.clk(clk), .D(D), .Q(Q), .preset(1'b0), .en(Enable), .reset(Clear));  // open: Qn
endmodule
